# Fritzing sketch esp8266_schematic (saved by Fritzing 1.0.0rc)
breadboards: 1

parts:
  SP1 = SPEAKER [package=pcb_mount_speaker]
  part = ESP8266 ESP-01 Upgraded WiFi Module [part_number=ESP8266]

nets:
  N1: SP1.+, part.GND
  N2: SP1.-, part.RXD
  N3: part.VCC, part.CH_PD

custom parts:
  ESP8266 ESP-01 Upgraded WiFi Module: Upgraded Version ESP-01,all Flash are upgraded to 1M byte.Also support Cloud service remote transmission.
